# Fritzing sketch NRF24L01_Connection (saved by Fritzing 0.9.3b)

parts:
  Part1 = Arduino Uno (Rev3)
  Part2 = Arduino Mega 2560 (Rev3)
  Part3 = NRF24L01+ Breakout Board
  Part4 = NRF24L01+ Breakout Board

nets:
  N1: Part1.D8, Part3.CS
  N2: Part1.D11_PWM/MOSI, Part3.MOSI
  N3: Part1.D12/MISO, Part3.MISO
  N4: Part1.D13/SCK, Part3.SCK
  N5: Part1.D7, Part3.CE
  3V3: Part1.3V3, Part3.VCC
  GND: Part1.GND, Part3.GND
  N6: Part2.D8_PWM, Part4.CS
  3V3_2: Part2.3V3, Part4.VCC
  GND_2: Part2.GND, Part4.GND
  N7: Part2.D7_PWM, Part4.CE
  N8: Part2.D50, Part4.MISO
  N9: Part2.D51, Part4.MOSI
  N10: Part2.D52, Part4.SCK

notes:
  1- GND
  2- 3.3v
  3- pin 7
  4- pin 8
  5- pin 13
  6- pin 11
  7- pin 12
  Arduino NANO/UNO
  1- GND
  2- 3.3v
  3- pin 7
  4- pin 8
  5- pin 52
  6- pin 51
  7- pin 50
  Arduino Mega/DUE
